# Fritzing sketch diagram (saved by Fritzing 0.9.3b)
breadboards: 1

parts:
  J1 = T Cobbler Plus
  YF-S201_Flow_Meter1 = YF-S201 Water Flow Meter
  YF-S201_Flow_Meter2 = YF-S201 Water Flow Meter
  YF-S201_Flow_Meter3 = YF-S201 Water Flow Meter
  YF-S201_Flow_Meter4 = YF-S201 Water Flow Meter
  OLED1 = 128x32 I2C Monochrome OLED Display
  DS1 = DS18B20 1-Wire Temperature Sensor [part_number=DS18B20]
  AM1 = AM2302 Humidity and Temperature Sensor
  S1 = Pushbutton [package="[THT]"]
  R1 = Resistor [tolerance=±5% resistance=10k package="2512 [SMD]"]
  R2 = Resistor [tolerance=±5% resistance=4.7k package="2512 [SMD]"]

nets:
  VCC: J1.3V3, YF-S201_Flow_Meter1.VCC, YF-S201_Flow_Meter2.VCC, YF-S201_Flow_Meter3.VCC, YF-S201_Flow_Meter4.VCC, OLED1.3.3V, DS1.VDD, AM1.VDD, S1.Pin_3, S1.Pin_4, R2.Pin_1
  N1: J1.SDA, OLED1.SDA
  N2: J1.SCL, OLED1.SCL
  N3: J1.#23, OLED1.RST
  N4: J1.#24, YF-S201_Flow_Meter2.SIG
  GND: J1.GND#19, YF-S201_Flow_Meter1.GND, YF-S201_Flow_Meter2.GND, YF-S201_Flow_Meter3.GND, YF-S201_Flow_Meter4.GND
  N5: J1.#25, YF-S201_Flow_Meter3.SIG
  GND_2: J1.GND#24, OLED1.GND, DS1.GND, AM1.GND, R1.Pin_1
  N6: J1.#5, YF-S201_Flow_Meter1.SIG
  N7: J1.#19, DS1.DQ, R2.Pin_0
  N8: J1.#16, S1.Pin_1, S1.Pin_2, R1.Pin_0
  N9: J1.#26, AM1.DATA
  N10: J1.#20, YF-S201_Flow_Meter4.SIG

custom parts:
  T Cobbler Plus: The T-Cobbler Plus is an add on prototyping board from Adafruit specifically designed for the Raspberry Pi B+ that can break out all those tasty power, GPIO, I2C and SPI pins from the 40-pin header onto a solderless breadboard. This set will make "cobbling together" prototypes with the Pi super easy. The T-Cobbler Plus can plug into any solderless breadboard.
  YF-S201 Water Flow Meter: The YF-S201 Flow Meter. The input voltage is 5V to 24V (DC).
